# Fritzing sketch knoba - Arduino Battery Power Supply - 2016 (saved by Fritzing 0.9.2b)
breadboards: 1

parts:
  CONN1 = USB connector [package=THT]
  VCC2 = Battery
  S1 = Toggle Switch [package=THT]
  VCC1 = Battery

nets:
  N1: CONN1.5V, S1.L1, S1.L2
  N2: CONN1.GND, VCC2.-, VCC2.+, S1.COM, VCC1.-, VCC1.+
