# Fritzing sketch knoba - Tool Throat LED Schematic - 2018 (saved by Fritzing 0.9.2b)
breadboards: 1

parts:
  V1 = AC Power [voltage=240 frequency=50]
  M1 = DC Motor
  Motor_start_/_run_capacitor = Ceramic Capacitor [capacitance=100nF package="100 mil [THT, multilayer]"]
  S1_-_Tool_Switch = SWITCH-DPDT [package=eg2211]
  LED_COB_240v_20w = LED - 5mm [color="Red (633nm)" package="5 mm [THT]"]
  Fuse_1a_240v = Fuse with Handler [part_number=Htc-15m]

nets:
  N1: V1.V+, S1_-_Tool_Switch.2, Fuse_1a_240v.Connector1
  N2: V1.V-, S1_-_Tool_Switch.5, LED_COB_240v_20w.cathode
  N3: M1.pin_1, Motor_start_/_run_capacitor.1, S1_-_Tool_Switch.3
  N4: M1.pin_2, Motor_start_/_run_capacitor.0, S1_-_Tool_Switch.6
  N5: LED_COB_240v_20w.anode, Fuse_1a_240v.Connector2
