# Fritzing sketch knoba - Workshop Smoke Alarm Schematic - 2018 (saved by Fritzing 0.9.2b)
breadboards: 1

parts:
  R1 = Resistor [tolerance=±5% resistance=470 package=THT]
  LED1 = LED - 5mm [color="Blue (505nm)" package="5 mm [THT]"]
  VCC1 = Battery block 9V
  S4 = Toggle Switch [package=THT]

nets:
  N1: R1.Pin_0, S4.L1
  N2: R1.Pin_1, LED1.anode
  GND: LED1.cathode, VCC1.-
  N3: VCC1.+, S4.COM
  Smoke Alarm Power: S4.L2
