# Fritzing sketch knoba - ac power supply - schematic - 2016 (saved by Fritzing 0.9.2b)

parts:
  F1_240v_2A = FUSE [package=fuse_5mm]
  F2_-_240v_1A = FUSE [package=fuse_5mm]
  U1_240vac_16vac_(multitap) = TRANSFORMER [package=transformer]
  D1 = Rectifier Diode [part_number=1N4001 package="300 mil [THT]"]
  C1_275v_0_33uF = Ceramic Capacitor [capacitance=100nF package="100 mil [THT, multilayer]"]
  R1 = Resistor [tolerance=±5% resistance=1k package=THT]
  S1_DPDT = Toggle Switch [package=THT]
  S2_DPDT = Toggle Switch [package=THT]
  sw1_-_6P1T_-_pin1 = Toggle Switch [package=THT]
  sw1_-_6P1T_-_pin2 = Toggle Switch [package=THT]
  sw1_-_6P1T_-_pin3 = Toggle Switch [package=THT]
  sw1_-_6P1T_-_pin4 = Toggle Switch [package=THT]
  sw1_-_6P1T_-_pin5 = Toggle Switch [package=THT]
  LED1 = LED - 5mm [color="Blue (525nm)" package="5 mm [THT]"]
  J1 = BANANA_CONN [package=banana_conn]
  J2 = BANANA_CONN [package=banana_conn]
  C2_400v_22uF = Ceramic Capacitor [capacitance=100nF package="100 mil [THT, multilayer]"]
  V1_240v_50Hz = AC Power [frequency=50 voltage=5]
  J3 = shrouded pin header, 6 pins [form="♂ (shrouded male)"]
  sw1_-_6P1T_-_pin6 = Toggle Switch [package=THT]
  R2 = Resistor [tolerance=±5% resistance=38k package=THT]
  Analog_Meter = DC Motor
  R3 = Resistor [tolerance=±5% resistance=560k package=THT]
  LED2 = LED - 5mm [color="White (6500K)" package="5 mm [THT]"]
  R4 = Resistor [tolerance=±5% resistance=220 package=THT]

nets:
  N1: F1_240v_2A.1, C1_275v_0_33uF.1, V1_240v_50Hz.V+, R3.Pin_1
  N2: F1_240v_2A.2, S1_DPDT.COM
  N3: F2_-_240v_1A.1, D1.cathode, sw1_-_6P1T_-_pin1.L1, sw1_-_6P1T_-_pin2.L1, sw1_-_6P1T_-_pin3.L1, sw1_-_6P1T_-_pin4.L1, sw1_-_6P1T_-_pin5.L1, J2.1, sw1_-_6P1T_-_pin6.L1
  N4: F2_-_240v_1A.2, J1.1, R2.Pin_0
  N5: U1_240vac_16vac_(multitap).1, R1.Pin_0, S1_DPDT.L1
  N6: U1_240vac_16vac_(multitap).2, S2_DPDT.L2, LED1.cathode, LED2.anode
  N7: U1_240vac_16vac_(multitap).3, J3.pin6, sw1_-_6P1T_-_pin6.COM
  N8: U1_240vac_16vac_(multitap).4, sw1_-_6P1T_-_pin1.COM, J3.pin1
  N9: D1.anode, Analog_Meter.pin_2
  N10: C1_275v_0_33uF.0, S2_DPDT.COM, V1_240v_50Hz.V-, R3.Pin_0
  N11: R1.Pin_1, C2_400v_22uF.0
  N12: sw1_-_6P1T_-_pin2.COM, J3.pin2
  N13: sw1_-_6P1T_-_pin3.COM, J3.pin3
  N14: sw1_-_6P1T_-_pin4.COM, J3.pin4
  N15: sw1_-_6P1T_-_pin5.COM, J3.pin5
  N16: LED1.anode, LED2.cathode, R4.Pin_1
  N17: C2_400v_22uF.1, R4.Pin_0
  N18: R2.Pin_1, Analog_Meter.pin_1
