# Fritzing sketch knoba - component tester schematic - 2016 (saved by Fritzing 0.9.2b)
circuit board: 8.52319cm x 7.97573cm
breadboards: 1

parts:
  J1_(Black_Probe) = BANANA_CONN [package=banana_conn]
  J2_(Red_Probe) = BANANA_CONN [package=banana_conn]
  U1_(X_Axis) = BNC [package=bnc]
  U2_(Y_Axis) = BNC [package=bnc]
  V1 = AC Power [voltage=240 frequency=50Hz]
  R1 = Resistor [tolerance=±5% resistance=270 package=THT]
  R2 = Resistor [tolerance=±5% resistance=91 package=THT]
  R3 = Resistor [tolerance=±5% resistance=1k package=THT]
  J3_(Scope_Gnd) = BANANA_CONN [package=banana_conn]
  C1 = Ceramic Capacitor [capacitance=0.22µF voltage=400V package="100 mil [THT, multilayer]"]
  R4 = Resistor [tolerance=±5% resistance=1k package=THT]
  D1 = Rectifier Diode [part_number=1N4004 package="300 mil [THT]"]
  F1 = FUSE [package=fuse_5mm]
  LED1 = LED - 5mm [color="Red (635nm)" package="5 mm [THT]"]
  U3_(40_1) = TRANSFORMER [package=transformer]

nets:
  GND: J1_(Black_Probe).1, U1_(X_Axis).GND, U2_(Y_Axis).GND, R3.Pin_1, J3_(Scope_Gnd).1
  N1: J2_(Red_Probe).1, U1_(X_Axis).OUT, R2.Pin_1, U3_(40_1).3
  N2: U2_(Y_Axis).OUT, R1.Pin_1, R2.Pin_0, R3.Pin_0
  N3: V1.V+, F1.1
  N4: V1.V-, D1.anode, LED1.cathode, U3_(40_1).2
  6.76V: R1.Pin_0, U3_(40_1).4
  N5: C1.0, F1.2, U3_(40_1).1
  N6: C1.1, R4.Pin_0
  N7: R4.Pin_1, D1.cathode, LED1.anode
