# Fritzing sketch knoba - electric guitar - 2017 (saved by Fritzing 0.9.2b)
breadboards: 1

parts:
  L1 = Inductor [package="400 mil [THT]"]
  J1 = female pin header, 2 pins [form="♀ (female)"]
  C1 = Ceramic Capacitor [capacitance=2.2µF voltage=16V package="100 mil [THT, multilayer]"]
  C2 = Ceramic Capacitor [capacitance=4.7µF voltage=16V package="100 mil [THT, multilayer]"]
  R1 = Rotary Potentiometer (Small) [maximum_resistance=500kΩ package=THT]
  R2 = Rotary Potentiometer (Small) [maximum_resistance=500kΩ package=THT]
  R3 = Rotary Potentiometer (Small) [maximum_resistance=250kΩ package=THT]
  L2 = Inductor [package="400 mil [THT]"]
  L3 = Inductor [package="400 mil [THT]"]
  part = Toggle Switch [package=THT]
  part_2 = Toggle Switch [package=THT]
  part_3 = Toggle Switch [package=THT]
  part_4 = Toggle Switch [package=THT]
  part_5 = Toggle Switch [package=THT]
  part_6 = Toggle Switch [package=THT]
  part_7 = Toggle Switch [package=THT]
  part_8 = Toggle Switch [package=THT]
  part_9 = Toggle Switch [package=THT]
  part_10 = Toggle Switch [package=THT]
  part_11 = Toggle Switch [package=THT]
  part_12 = Toggle Switch [package=THT]

nets:
  N1: L1.pin_0, part_2.L1, part_4.L2
  N2: L1.pin_1, part.L1, part_3.L2
  GND: J1.pin1, C1.0, C2.0, R3.leg2, part_3.L1, part_8.L1
  N3: J1.pin2, R3.wiper
  N4: R1.leg1, R2.leg1, R3.leg1, part_4.L1, part_6.L1, part_10.L2
  N5: L2.pin_0, part_6.L2, part_7.L1
  N6: L2.pin_1, part_5.L1, part_8.L2
  N7: L3.pin_0, part_9.L2, part_11.L1
  N8: L3.pin_1, part_10.L1, part_12.L2
  N9: part_7.L2, part_12.L1

notes:
  Guitar Wiring, 3 single coils, phase reversal (3 dpdt's), high & low pass tones., 1.0
